# Fritzing sketch esp (saved by Fritzing 0.9.4)
breadboards: 2

parts:
  Компонент1 = Arduino Mega 2560 (Rev3)
  Espessif_Serial_Wifi_Modul_1 = ESP8266 ESP01 [part_number=ESP8266 package=THT]

nets:
  GND: Компонент1.GND, Espessif_Serial_Wifi_Modul_1.GND
  3V3: Компонент1.3V3, Espessif_Serial_Wifi_Modul_1.VCC, Espessif_Serial_Wifi_Modul_1.CH_PD
  N1: Компонент1.D0_RX0, Espessif_Serial_Wifi_Modul_1.RXD
  N2: Компонент1.D1_TX0, Espessif_Serial_Wifi_Modul_1.TXD

custom parts:
  ESP8266 ESP01: Generic WiFi Module based on the ESP8266 with onboard PCB antenna and UART communications
