# Fritzing sketch termo-meter (saved by Fritzing 0.9.4)

parts:
  LCD1 = LCD screen
  Компонент1 = Arduino Mega 2560 (Rev3)
  PCB2 = RTC_DS1302_module
  LCM1602_IIC1 = LCM1602 IIC [part_number="LCM1602 IIC" chip_label="LCM1602 IIC" package="DIP (Dual Inline) [THT]"]
  Mod1 = KY-015 Temperature & Humidity Sensor Module [package="Breakout board"]  # not connected

nets:
  VSS: LCD1.VSS, LCM1602_IIC1.VSS
  VDD: LCD1.VDD, LCM1602_IIC1.VDD
  N1: LCD1.V0, LCM1602_IIC1.V0
  N2: LCD1.RS, LCM1602_IIC1.RS
  N3: LCD1.R/W, LCM1602_IIC1.RW
  N4: LCD1.E, LCM1602_IIC1.E
  N5: LCD1.DB0, LCM1602_IIC1.D0
  N6: LCD1.DB1, LCM1602_IIC1.D1
  N7: LCD1.DB2, LCM1602_IIC1.D2
  N8: LCD1.DB3, LCM1602_IIC1.D3
  N9: LCD1.DB4, LCM1602_IIC1.D4
  N10: LCD1.DB5, LCM1602_IIC1.D5
  N11: LCD1.DB6, LCM1602_IIC1.D6
  N12: LCD1.DB7, LCM1602_IIC1.D7
  N13: LCD1.LED+, LCM1602_IIC1.A
  N14: LCD1.LED-, LCM1602_IIC1.K
  N15: Компонент1.D21/SCL, LCM1602_IIC1.SCL
  N16: Компонент1.D20/SDA, LCM1602_IIC1.SDA
  N17: Компонент1.D19/RX1, LCM1602_IIC1.VCC
  N18: Компонент1.D18/TX1, LCM1602_IIC1.GND
  N19: Компонент1.D45, PCB2.VCC
  N20: Компонент1.D47, PCB2.GND
  N21: Компонент1.D49, PCB2.CLK
  N22: Компонент1.D51, PCB2.DAT
  N23: Компонент1.D53, PCB2.RST

custom parts:
  RTC_DS1302_module: Arduino module DS1302 SPI Real Time Clock
  LCM1602 IIC: I2C-Module to use a 1602 or 2004 LCD on with the wire.h libory Serial LCD Modul
  KY-015 Temperature & Humidity Sensor Module: KY-015 temperature and humidity sensor module, provides a low-latency serial interface to measure humidity and temperature.
